// Logisim project cpu_debuged.circ as structural Verilog: 4 circuits, main circuit ALU
module ALU (
  input  [7:0] A,
  input  [7:0] B,
  input  OP,
  output o,
  output o_2,
  output o_3,
  output [7:0] R,
  output Overflow
);

  wire [7:0] multiplexer_1_out, negator_1_out;

  Negator negator_1 (.in(B), .out(negator_1_out));
  Multiplexer #(.width(8)) multiplexer_1 (.in0(B), .in1(negator_1_out), .out(multiplexer_1_out), .sel(OP));  // open: en
  Adder adder_1 (.a(multiplexer_1_out), .b(A), .out(R), .cout(Overflow));  // open: cin
  Comparator comparator_1 (.a(B), .b(A), .gt(o), .eq(o_2), .lt(o_3));
endmodule

module Decoder (
  input  [7:0] in_1,
  output _00,
  output _01,
  output _02,
  output _03,
  output _04,
  output _07,
  output _08,
  output _09,
  output _0A,
  output _0B,
  output _0D
);

  wire not_1_out, not_2_out, not_3_out, not_4_out, not_5_out, not_6_out, not_7_out, not_8_out;

  not not_1 (not_1_out, in_1[0]);
  not not_2 (not_2_out, in_1[1]);
  not not_3 (not_3_out, in_1[2]);
  not not_4 (not_4_out, in_1[3]);
  not not_5 (not_5_out, in_1[4]);
  not not_6 (not_6_out, in_1[5]);
  not not_7 (not_7_out, in_1[6]);
  not not_8 (not_8_out, in_1[7]);
  and and_1 (_00, not_1_out, not_2_out, not_3_out, not_4_out, not_5_out, not_6_out, not_7_out, not_8_out);
  and and_2 (_01, in_1[0], not_2_out, not_3_out, not_4_out, not_5_out, not_6_out, not_7_out, not_8_out);
  and and_3 (_02, not_1_out, in_1[1], not_3_out, not_4_out, not_5_out, not_6_out, not_7_out, not_8_out);
  and and_4 (_03, in_1[0], in_1[1], not_3_out, not_4_out, not_5_out, not_6_out, not_7_out, not_8_out);
  and and_5 (_04, not_1_out, not_2_out, in_1[2], not_4_out, not_5_out, not_6_out, not_7_out, not_8_out);
  and and_6 (_07, in_1[0], in_1[1], in_1[2], not_4_out, not_5_out, not_6_out, not_7_out, not_8_out);
  and and_7 (_08, not_1_out, not_2_out, not_3_out, in_1[3], not_5_out, not_6_out, not_7_out, not_8_out);
  and and_8 (_09, in_1[0], not_2_out, not_3_out, in_1[3], not_5_out, not_6_out, not_7_out, not_8_out);
  and and_9 (_0A, not_1_out, in_1[1], not_3_out, in_1[3], not_5_out, not_6_out, not_7_out, not_8_out);
  and and_10 (_0B, in_1[0], in_1[1], not_3_out, in_1[3], not_5_out, not_6_out, not_7_out, not_8_out);
  and and_11 (_0D, in_1[0], not_2_out, in_1[2], in_1[3], not_5_out, not_6_out, not_7_out, not_8_out);
endmodule

module Steper (
  input  clk,
  output Step_1,
  output Step_2
);

  Counter #(.width(1), .max('h1)) counter_1 (.count(1'b1), .Q(Step_2), .clk(clk));  // open: load, D, carry, clr
  not not_1 (Step_1, Step_2);
endmodule

module main (
  input  [15:0] User_Input
);

  wire _00, _0A, _0B, _0D, _01, _02, _03, _04, _07, _08, _09, ACC___USER, alu_1_o_2, alu_1_o_3, and_1_out,
       and_2_out, and_3_out, and_13_out, Clk, Desvio, Enable_ACC, Enable_IR, IR___ACC, IR___PC, not_1_out,
       not_2_out, OP, or_1_out, or_2_out, or_3_out, or_4_out, or_5_out, or_6_out, or_7_out, RAM___ULA,
       Step_2, Store_RAM, ULA___OUT;
  wire [7:0] ACC_INST, ACC_OUT, IR_AD_OUT, IR_INST_OUT, multiplexer_1_out, multiplexer_2_out, PC_q, ULA_B,
       ULA_R;
  wire [15:0] demultiplexer_1_out0, demultiplexer_1_out1, multiplexer_3_out, ram_1_data, RAM_INPUT, RAM_OUT;
  wire [15:8] demultiplexer_2_out0;

  not not_1 (not_1_out, _09);
  not not_2 (not_2_out, Desvio);
  and and_1 (and_1_out, not_1_out, not_2_out, Step_2);
  Decoder decoder_1 (
    .in_1(IR_INST_OUT), ._00(_00), ._01(_01), ._02(_02), ._03(_03), ._04(_04), ._07(_07), ._08(_08),
    ._09(_09), ._0A(_0A), ._0B(_0B), ._0D(_0D));
  Counter PC (.load(Desvio), .D(IR_AD_OUT), .count(and_1_out), .Q(PC_q), .clk(Clk));  // open: carry, clr
  Steper steper_1 (.Step_2(Step_2), .clk(Clk));  // open: Step_1
  Multiplexer #(.width(8), .enable("false")) multiplexer_1 (
    .in0(ULA_B), .in1({8{1'b0}}), .out(multiplexer_1_out), .sel(_0B));
  ALU alu_1 (
    .A(ACC_OUT), .OP(OP), .o_2(alu_1_o_2), .o_3(alu_1_o_3), .R(ULA_R), .B(multiplexer_1_out));  // open: o, Overflow
  Multiplexer #(.width(8), .enable("false")) multiplexer_2 (
    .in0(PC_q), .in1(IR_AD_OUT), .out(multiplexer_2_out), .sel(IR___PC));
  Clock clock_1 (.out(Clk));
  and and_2 (and_2_out, _0D, alu_1_o_2);
  and and_3 (and_3_out, _0B, alu_1_o_3);
  or or_1 (or_1_out, _01, _02, _03);
  or or_2 (or_2_out, _04, _07, _08);
  and and_4 (IR___ACC, _01, Step_2);
  or or_3 (or_3_out, _07, _02);
  RAM #(.dataWidth(16), .bus("separate")) ram_1 (
    .addr(multiplexer_2_out), .din(RAM_INPUT), .data(ram_1_data), .str(Store_RAM), .clk(Clk), .ld(1'b1));  // open: sel, clr
  or or_4 (or_4_out, or_1_out, or_2_out);
  or or_5 (or_5_out, and_2_out, _0A, and_3_out);
  Demultiplexer #(.width(16), .enable("false")) demultiplexer_1 (
    .out0(demultiplexer_1_out0), .out1(demultiplexer_1_out1), .in(ram_1_data), .sel(IR___ACC));
  and and_5 (IR___PC, or_4_out, Step_2);
  and and_6 (Desvio, or_5_out, Step_2);
  and and_7 (Store_RAM, or_3_out, Step_2);
  Register #(.width(16)) IR (
    .D(demultiplexer_1_out0), .en(Enable_IR), .Q({IR_INST_OUT, IR_AD_OUT}), .clk(Clk));  // open: clr
  Demultiplexer #(.width(16), .enable("false")) demultiplexer_2 (
    .out0({demultiplexer_2_out0, ULA_B}), .out1(RAM_OUT), .in(ram_1_data), .sel(ULA___OUT));
  Multiplexer #(.width(16), .enable("false")) multiplexer_3 (
    .in0(demultiplexer_1_out1), .in1({ACC_INST, ULA_R}), .out(multiplexer_3_out), .sel(RAM___ULA));
  or or_6 (or_6_out, _01, _04, _03);
  or or_7 (or_7_out, _04, _03);
  Register #(.width(16)) ACC (.D(multiplexer_3_out), .en(Enable_ACC), .Q({ACC_INST, ACC_OUT}), .clk(Clk));  // open: clr
  and and_8 (Enable_ACC, or_6_out, Step_2);
  and and_9 (RAM___ULA, or_7_out, Step_2);
  and and_10 (OP, _04, Step_2);
  and and_11 (ACC___USER, _07, Step_2);
  and and_12 (ULA___OUT, _08, Step_2);
  not not_3 (Enable_IR, and_13_out);
  and and_13 (and_13_out, _08, Step_2);
  Multiplexer #(.width(16), .enable("false")) multiplexer_4 (
    .in0({ACC_INST, ACC_OUT}), .in1(User_Input), .out(RAM_INPUT), .sel(ACC___USER));
  Hex_Digit_Display hex_digit_display_1 (.value(RAM_OUT[11:8]));  // open: dp
  Hex_Digit_Display hex_digit_display_2 (.value(RAM_OUT[15:12]));  // open: dp
  Hex_Digit_Display hex_digit_display_3 (.value(RAM_OUT[7:4]));  // open: dp
  Hex_Digit_Display hex_digit_display_4 (.value(RAM_OUT[3:0]));  // open: dp

  // Other names for the same wires on the sheet: ULA_A[7:0] = ACC_OUT; ACC_OUT[15:8] = ACC_INST
endmodule
